# Fritzing sketch Fritzing file (saved by Fritzing 0.9.3b)
breadboards: 1

parts:
  Part1 = Arduino Uno (Rev3)
  J1 = Basic Servo
  VCC1 = Battery block 9V
  hc-sr1 = HC-SR04

nets:
  N1: Part1.D9_PWM, hc-sr1.Trig
  N2: Part1.D10_PWM/SS, hc-sr1.Echo
  N3: Part1.D6_PWM, J1.pulse
  5V: Part1.5V, hc-sr1.VCC
  GND: Part1.GND, J1.gnd, VCC1.-, hc-sr1.GND
  N4: Part1.VIN, VCC1.+

custom parts:
  HC-SR04: This is a HC-SR04 Distance Sensor. This economical sensor provides 2cm to 400cm of non-contact measurement functionality with a ranging accuracy that can reach up to 3mm. Each HC-SR04 module includes an ultrasonic transmitter, a receiver and a control circuit. There are only four pins that you need to worry about on the HC-SR04: VCC (Power), Trig (Trigger), Echo (Receive), and GND (Ground).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
